// Logisim project lab2.circ as structural Verilog: 1 circuit, main circuit main
module main (
  input  in_1,
  input  in_2,
  input  in_3,
  input  in_4,
  input  in_5,
  input  in_6,
  input  in_7,
  input  in_8,
  input  in_9,
  input  in_10,
  input  in_11,
  input  in_12,
  input  in_13,
  input  in_14,
  input  in_15,
  input  in_16,
  input  in_17,
  input  in_18,
  input  in_19,
  input  in_20,
  input  in_21,
  input  in_22,
  input  in_23,
  input  in_24,
  input  in_25,
  input  in_26,
  input  in_27,
  input  in_28,
  input  in_29,
  input  in_30,
  input  in_31,
  input  in_32,
  input  in_33,
  input  in_34,
  input  in_35,
  input  in_36,
  input  in_37,
  input  in_38,
  input  in_39,
  input  in_40,
  input  in_41
);

  wire and_1_out, and_2_out, and_3_out, and_4_out, and_5_out, and_6_out, and_7_out, and_8_out,
       multiplexer_1_out, multiplexer_2_out, multiplexer_3_out, multiplexer_4_out, multiplexer_5_out,
       multiplexer_6_out, multiplexer_7_out, not_1_out, not_2_out, not_3_out, or_1_out, or_2_out, or_3_out,
       or_4_out;
  wire [2:0] priority_encoder_1_out;

  not not_1 (not_1_out, in_13);
  not not_2 (not_2_out, in_17);
  not not_3 (not_3_out, in_20);
  or or_1 (or_1_out, in_30, in_36, in_39, in_41);
  or or_2 (or_2_out, in_33, in_36, in_40, in_41);
  or or_3 (or_3_out, in_38, in_39, in_40, in_41);
  and and_1 (and_1_out, in_2, not_1_out, not_2_out, not_3_out);
  and and_2 (and_2_out, in_8, not_1_out, not_2_out, in_20);
  and and_3 (and_3_out, in_14, not_1_out, in_17, not_3_out);
  and and_4 (and_4_out, not_1_out, in_17, in_20, in_22);
  and and_5 (and_5_out, in_23, in_13, not_2_out, not_3_out);
  and and_6 (and_6_out, in_13, not_2_out, in_20, in_24);
  and and_7 (and_7_out, in_13, in_17, not_3_out, in_25);
  and and_8 (and_8_out, in_20, in_17, in_13, in_26);
  LED led_1 (.in(or_1_out));
  LED led_2 (.in(or_2_out));
  LED led_3 (.in(or_3_out));
  or or_4 (or_4_out, and_1_out, and_2_out, and_3_out, and_4_out, and_5_out, and_6_out, and_7_out, and_8_out);
  LED led_4 (.in(or_4_out));
  Priority_Encoder priority_encoder_1 (
    .in0(in_27), .in1(in_28), .in2(in_29), .in3(in_31), .in4(in_32), .in5(in_34), .in6(in_37), .in7(in_35),
    .out(priority_encoder_1_out));  // open: en_in, gs, en_out
  LED led_5 (.in(priority_encoder_1_out[0]));
  LED led_6 (.in(priority_encoder_1_out[2]));
  LED led_7 (.in(priority_encoder_1_out[1]));
  Multiplexer multiplexer_1 (.in0(in_1), .out(multiplexer_1_out), .sel(in_4));  // open: in1
  Multiplexer multiplexer_2 (.in0(in_5), .in1(in_7), .out(multiplexer_2_out), .sel(in_9));
  Multiplexer multiplexer_3 (.in0(in_11), .in1(in_12), .out(multiplexer_3_out), .sel(in_15));
  Multiplexer multiplexer_4 (.in0(in_18), .in1(in_19), .out(multiplexer_4_out), .sel(in_21));
  Multiplexer multiplexer_5 (.in0(multiplexer_1_out), .in1(multiplexer_2_out), .out(multiplexer_5_out), .sel(in_6));
  Multiplexer multiplexer_6 (.in0(multiplexer_3_out), .in1(multiplexer_4_out), .out(multiplexer_6_out), .sel(in_16));
  Multiplexer multiplexer_7 (.in0(multiplexer_5_out), .in1(multiplexer_6_out), .out(multiplexer_7_out), .sel(in_10));
  LED led_8 (.in(multiplexer_7_out));

  // Notes on the sheet:
  //   Multiplexer 
  //   Encoder
  //   Multiplexer
endmodule
