// Logisim project lab3.circ as structural Verilog: 1 circuit, main circuit main
module main (
  input  in_1,
  input  in_2,
  input  in_3,
  input  in_4,
  input  in_5,
  input  in_6,
  input  in_7,
  input  in_8
);

  wire clock_1_out, nand_1_out, nand_2_out, nand_3_out, nand_4_out, nand_5_out, nand_6_out, nand_7_out,
       nand_8_out, nand_9_out, nand_10_out, nand_11_out, nand_12_out, nand_13_out, nand_14_out, nand_15_out,
       nand_16_out, nand_17_out, nand_18_out, nand_19_out, nand_20_out, nand_21_out, nand_22_out,
       nand_23_out, nand_24_out, nand_25_out, nand_26_out, nand_27_out, nand_28_out, nand_29_out,
       nand_31_out, nand_33_out, nand_35_out, nand_36_out;

  nand nand_1 (nand_1_out, in_5, in_6);
  nand nand_2 (nand_2_out, in_1, in_1);
  nand nand_3 (nand_3_out, in_3, in_4);
  nand nand_4 (nand_4_out, in_7, in_8);
  nand nand_5 (nand_5_out, in_1, nand_2_out);
  nand nand_6 (nand_6_out, nand_2_out, in_1);
  nand nand_7 (nand_7_out, in_3, nand_3_out);
  nand nand_8 (nand_8_out, nand_3_out, in_4);
  nand nand_9 (nand_9_out, in_5, nand_1_out);
  nand nand_10 (nand_10_out, nand_1_out, in_6);
  nand nand_11 (nand_11_out, in_7, nand_4_out);
  nand nand_12 (nand_12_out, nand_4_out, in_8);
  nand nand_13 (nand_13_out, nand_5_out, nand_6_out);
  Clock clock_1 (.out(clock_1_out));
  nand nand_14 (nand_14_out, nand_7_out, nand_8_out);
  nand nand_15 (nand_15_out, nand_9_out, nand_10_out);
  nand nand_16 (nand_16_out, nand_11_out, nand_12_out);
  nand nand_17 (nand_17_out, nand_13_out, clock_1_out);
  nand nand_18 (nand_18_out, nand_14_out, nand_26_out);
  nand nand_19 (nand_19_out, nand_15_out, nand_22_out);
  nand nand_20 (nand_20_out, nand_16_out, nand_28_out);
  nand nand_21 (nand_21_out, nand_15_out, nand_19_out);
  nand nand_22 (nand_22_out, nand_19_out, nand_22_out);
  nand nand_23 (nand_23_out, nand_13_out, nand_17_out);
  nand nand_24 (nand_24_out, nand_17_out, clock_1_out);
  nand nand_25 (nand_25_out, nand_14_out, nand_18_out);
  nand nand_26 (nand_26_out, nand_18_out, nand_26_out);
  nand nand_27 (nand_27_out, nand_16_out, nand_20_out);
  nand nand_28 (nand_28_out, nand_20_out, nand_28_out);
  nand nand_29 (nand_29_out, nand_23_out, nand_24_out);
  LED led_1 (.in(nand_29_out));
  nand nand_30 (nand_26_out, nand_17_out, nand_2_out);
  LED led_2 (.in(nand_26_out));
  nand nand_31 (nand_31_out, nand_25_out, nand_26_out);
  LED led_3 (.in(nand_31_out));
  nand nand_32 (nand_22_out, nand_18_out, nand_3_out);
  LED led_4 (.in(nand_22_out));
  nand nand_33 (nand_33_out, nand_21_out, nand_22_out);
  LED led_5 (.in(nand_33_out));
  nand nand_34 (nand_28_out, nand_19_out, nand_1_out);
  LED led_6 (.in(nand_28_out));
  nand nand_35 (nand_35_out, nand_27_out, nand_28_out);
  LED led_7 (.in(nand_35_out));
  nand nand_36 (nand_36_out, nand_20_out, nand_4_out);
  LED led_8 (.in(nand_36_out));
  // Digital_Oscilloscope digital_oscilloscope_1: pin names not known; wires that end beside it: nand_35_out, nand_31_out, nand_31_out, nand_33_out, nand_35_out, nand_36_out, nand_29_out

  assign in_2 = in_1;
endmodule
