// Logisim project lab6.circ as structural Verilog: 1 circuit, main circuit main
module main (
  input  [3:0] in_1,
  input  in_2,
  input  in_3,
  input  [3:0] in_4,
  input  in_5,
  input  [3:0] in_6,
  input  [1:0] in_7,
  input  in_8,
  input  [3:0] in_9,
  input  in_10
);

  wire clock_1_out;
  wire [3:0] multiplexer_1_out, multiplexer_2_out, R0_q, R1_q, R2_q, R3_q;

  Clock clock_1 (.out(clock_1_out));
  Multiplexer #(.width(4)) multiplexer_1 (.in0(multiplexer_2_out), .in1(in_1), .out(multiplexer_1_out), .sel(in_2));
  Register #(.width(4)) R0 (.D(multiplexer_1_out), .en(in_3), .clk(clock_1_out), .Q(R0_q));  // open: clr
  Register #(.width(4)) R1 (.D(in_4), .en(in_5), .clk(clock_1_out), .Q(R1_q));  // open: clr
  Register #(.width(4)) R2 (.D(in_6), .en(in_8), .clk(clock_1_out), .Q(R2_q));  // open: clr
  Register #(.width(4)) R3 (.D(in_9), .en(in_10), .clk(clock_1_out), .Q(R3_q));  // open: clr
  Multiplexer #(.select(2), .width(4)) multiplexer_2 (
    .in0(R0_q), .in1(R1_q), .in2(R2_q), .in3(R3_q), .out(multiplexer_2_out), .sel(in_7));
  Hex_Digit_Display hex_digit_display_1 (.value(multiplexer_2_out));  // open: dp
endmodule
