// Logisim project lab1.circ as structural Verilog: 1 circuit, main circuit main
module main (
  input  in_1,
  input  in_2,
  input  in_3,
  input  in_4,
  input  in_5,
  input  in_6,
  input  in_7,
  input  in_8,
  input  in_9,
  input  in_10,
  input  in_11
);

  wire and_1_out, and_2_out, and_3_out, and_4_out, and_5_out, and_6_out, and_7_out, and_8_out, and_9_out,
       and_10_out, clock_1_out, clock_2_out, clock_3_out, clock_4_out, clock_5_out, clock_6_out, clock_7_out,
       nand_1_out, nand_2_out, nand_3_out, nand_4_out, nand_5_out, nand_6_out, nand_7_out, nand_8_out,
       nand_9_out, nand_10_out, nand_11_out, nand_12_out, nand_13_out, nand_14_out, or_1_out, or_2_out,
       or_3_out, or_4_out, xor_1_out, xor_2_out, xor_3_out, xor_4_out, xor_5_out, xor_6_out, xor_7_out,
       xor_8_out, xor_9_out, xor_10_out;

  Clock clock_1 (.out(clock_1_out));
  Clock clock_2 (.out(clock_2_out));
  Clock clock_3 (.out(clock_3_out));
  Clock clock_4 (.out(clock_4_out));
  Clock clock_5 (.out(clock_5_out));
  and and_1 (and_1_out, clock_3_out, clock_4_out);
  xor xor_1 (xor_1_out, in_4, in_5);
  xor xor_2 (xor_2_out, clock_1_out, clock_2_out);
  LED led_1 (.in(xor_2_out));
  xor xor_3 (xor_3_out, clock_3_out, clock_4_out);
  and and_2 (and_2_out, clock_1_out, clock_2_out);
  LED led_2 (.in(and_2_out));
  xor xor_4 (xor_4_out, xor_3_out, clock_5_out);
  and and_3 (and_3_out, in_4, in_5);
  LED led_3 (.in(xor_4_out));
  xor xor_5 (xor_5_out, in_6, in_7);
  and and_4 (and_4_out, in_6, in_7);
  and and_5 (and_5_out, xor_3_out, clock_5_out);
  // Digital_Oscilloscope digital_oscilloscope_1: pin names not known; wires that end beside it: xor_1_out
  Clock clock_6 (.out(clock_6_out));
  Clock clock_7 (.out(clock_7_out));
  xor xor_6 (xor_6_out, xor_5_out, and_3_out);
  and and_6 (and_6_out, xor_5_out, and_3_out);
  xor xor_7 (xor_7_out, in_8, in_9);
  and and_7 (and_7_out, in_8, in_9);
  nand nand_1 (nand_1_out, clock_6_out, clock_7_out);
  or or_1 (or_1_out, and_5_out, and_1_out);
  LED led_4 (.in(or_1_out));
  xor xor_8 (xor_8_out, xor_7_out, or_2_out);
  nand nand_2 (nand_2_out, clock_6_out, nand_1_out);
  nand nand_3 (nand_3_out, nand_1_out, clock_7_out);
  // Digital_Oscilloscope digital_oscilloscope_2: pin names not known; wires that end beside it: xor_6_out
  or or_2 (or_2_out, and_6_out, and_4_out);
  and and_8 (and_8_out, xor_7_out, or_2_out);
  nand nand_4 (nand_4_out, nand_2_out, nand_3_out);
  nand nand_5 (nand_5_out, in_1, in_2);
  // Digital_Oscilloscope digital_oscilloscope_3: pin names not known; wires that end beside it: xor_8_out
  and and_9 (and_9_out, in_10, in_11);
  nand nand_6 (nand_6_out, nand_1_out, nand_1_out);
  nand nand_7 (nand_7_out, in_1, nand_5_out);
  nand nand_8 (nand_8_out, nand_5_out, in_2);
  xor xor_9 (xor_9_out, in_10, in_11);
  // Digital_Oscilloscope digital_oscilloscope_4: pin names not known; wires that end beside it: nand_4_out
  or or_3 (or_3_out, and_8_out, and_7_out);
  xor xor_10 (xor_10_out, xor_9_out, or_3_out);
  nand nand_9 (nand_9_out, nand_7_out, nand_8_out);
  nand nand_10 (nand_10_out, nand_9_out, in_3);
  // Digital_Oscilloscope digital_oscilloscope_5: pin names not known; wires that end beside it: xor_10_out
  and and_10 (and_10_out, xor_9_out, or_3_out);
  // Digital_Oscilloscope digital_oscilloscope_6: pin names not known; wires that end beside it: nand_6_out
  nand nand_11 (nand_11_out, nand_9_out, nand_10_out);
  nand nand_12 (nand_12_out, nand_10_out, in_3);
  nand nand_13 (nand_13_out, nand_11_out, nand_12_out);
  // Digital_Oscilloscope digital_oscilloscope_7: pin names not known; wires that end beside it: nand_13_out
  nand nand_14 (nand_14_out, nand_10_out, nand_5_out);
  or or_4 (or_4_out, and_10_out, and_9_out);
  // Digital_Oscilloscope digital_oscilloscope_8: pin names not known; wires that end beside it: or_4_out
  // Digital_Oscilloscope digital_oscilloscope_9: pin names not known; wires that end beside it: nand_14_out

  // Notes on the sheet:
  //   half Adder
  //   Full Adder
  //   4 Bit Adder
  //   Half Adder
  //   Full Adder
endmodule
